# Fritzing sketch fritzing (saved by Fritzing 0.9.3b)

parts:
  Componente1 = Arduino Uno (Rev3)
  R1 = PHOTOCELL [package=photocell-kit]

nets:
  N1: Componente1.D5_PWM, R1.P$2
  N2: Componente1.5V, R1.P$1

// code stored in the sketch: Untitled.ino
#include <Servo.h>

int laserPin = 10;          //Laser pin set up
int buttonPin = 3;          //sets up button pin
int HoriPos = 10;           //Declare and initialise the horizontial pos variable.
int VertPos = 0;            //Declare and initialise the vertical pos variable.
int servoHoriPin = 7;       //Decalre horizontal servo pin.
int servoVertPin = 5;       //Decalre vertical servo pin.
int servoDelay = 25;        //Set delay for servo movemenet. 
int HoriPotRead;            //Sets up pot reading vari
int VertPotRead;            //Sets up pot reading vari
int buttonState = 0;        //Sets up empty button state var
int HoriPotPin = A0;        //Sets pot to pin A0
int VertPotPin = A5;        //Sets pot to pin A0

Servo servoHori;      // Names servo as horizontal axis

Servo servoVert;      // Names servo as Vertical axis

void setup(){
  
    Serial.begin(9600);           //Starts serial window
    
    servoHori.attach(servoHoriPin);   //Attaches servo to pin as a servo
    servoVert.attach(servoVertPin);   //Attaches servo to pin as a servo

    pinMode(buttonPin, INPUT_PULLUP); //Sets button pin as a pullup resisted input
    pinMode(laserPin, OUTPUT);        //Sets the laser pin as an output
}

void loop() {
  
  HoriPotRead = analogRead(HoriPotPin); //Read Hori potentiomter
  VertPotRead = analogRead(VertPotPin); //Read Vert pot

  buttonState = digitalRead(buttonPin); //Reads the state of the pin
    
  HoriPos = map(HoriPotRead, 0,1023,10,170);  //mapping Hori pot reading of 0-1023 to 10-170 for the hori servo
  VertPos = map(VertPotRead, 0,1023,0,80);    //mapping the vert pot reading of 0-1023 to 0-80 for the vert servo


  
  Serial.print(" Hori pot reading is: ");   //Printing vals to monitor
  Serial.print(HoriPotRead);
  
    
  Serial.print(" hori pos is: ");
  Serial.print(HoriPos);
  
  Serial.print(" Vert pot reading is: ");   //Printing vals to monitor
  Serial.print(VertPotRead);
  
  Serial.print(" vert pos is: ");
  Serial.print(VertPos);

  Serial.print(" Button State is: ");
  Serial.println(buttonState);
  
  if(buttonState == HIGH)                   //If else condition deciding if the Laser diode should be on or off. 
  {
    digitalWrite(laserPin, LOW);            // Button normally reads HIGH and LOW when pushed.
  }
  else
  {
    digitalWrite(laserPin, HIGH);
  }

  
  servoHori.write(HoriPos);                 //Writing values to the pos pins
  servoVert.write(VertPos);
  
  
  
  
  
}
